// Digital circuit ALU-shift-step.dig as structural Verilog
module ALU_shift_step (
  input  CLK,
  input  nCLK,
  input  nRESET,
  input  nEN,
  output SH_LOADLEN,
  output nSH_OUTPUT,
  output SH_RESET
);

  wire [3:0] counter_1_out;

  Counter #(.Bits(4)) counter_1 (.en(~nEN), .C(nCLK), .clr(~nRESET), .out(counter_1_out));  // open: ovf
  LookUpTable #(.Bits(3)) lookuptable_1 (
    .in0(counter_1_out[0]), .in1(counter_1_out[1]), .in2(counter_1_out[2]), .in3(counter_1_out[3]),
    .out({nSH_OUTPUT, SH_RESET, SH_LOADLEN}));

  // Notes on the sheet:
  //   contents of lookuptable_1 (hex, n*v repeats v):
  //   5,5,5,5,6,4,4,4,4
endmodule

/* Test case:
CLK  ~CLK  ~EN  ~RESET    SH-LOADLEN  SH-RESET  ~{SH-OUTPUT}

#0
0    1     0    0         1           0         1
1    0     0    0         1           0         1

#1
0    1     0    1         1           0         1
1    0     0    1         1           0         1

#2
0    1     0    1         1           0         1
1    0     0    1         1           0         1

#3
0    1     0    1         1           0         1
1    0     0    1         1           0         1

#4
0    1     0    1         0           1         1
1    0     0    1         0           1         1

#5
0    1     0    1         0           0         1
1    0     0    1         0           0         1

#6
0    1     0    1         0           0         1
1    0     0    1         0           0         1

#7
0    1     0    1         0           0         1
1    0     0    1         0           0         1

#8
0    1     0    1         0           0         1
1    0     0    1         0           0         1

#9
0    1     0    1         0           0         0
1    0     0    1         0           0         0

#10
0    1     0    1         0           0         0
1    0     0    1         0           0         0

#11
0    1     0    1         0           0         0
1    0     0    1         0           0         0

#12
0    1     0    1         0           0         0
1    0     0    1         0           0         0
*/
