// Digital circuit ALU-shifter.dig as structural Verilog
module ALU_shifter (
  input  CLK,
  input  IN_SH,
  input  LENIN_SH,
  input  nLA,
  input  LOADLEN_SH,
  input  nOUTPUT_SH,
  input  RESET_SH,
  output OUT_SH,
  output [5:0] DLEN
);

  wire and_1_out, d_ff_as_1_q, multiplexer_1_out;

  and and_1 (and_1_out, nOUTPUT_SH, CLK);
  Multiplexer multiplexer_1 (.sel(LOADLEN_SH), .in_0(IN_SH), .in_1(LENIN_SH), .out(multiplexer_1_out));
  D_FF_AS d_ff_as_1 (.Set(1'b0), .D(IN_SH), .C(and_1_out), .Clr(~nLA), .Q(d_ff_as_1_q));  // open: nQ
  _74HC595 _74hc595_1 (
    .SER(OUT_SH), .SRCLK(CLK), .nSRCLR(1'b1), .RCLK(RESET_SH), .nOE(LOADLEN_SH), .VCC(1'b1), .GND(1'b0),
    .QH(DLEN[0]), .QG(DLEN[1]), .QF(DLEN[2]), .QE(DLEN[3]), .QD(DLEN[4]), .QC(DLEN[5]));  // open: QB, QA, QH_2
  PullUp pullup_1 (.out(DLEN[4]));
  PullDown pulldown_1 (.out(DLEN[5]));
  PullUp pullup_2 (.out(DLEN[0]));
  PullUp pullup_3 (.out(DLEN[1]));
  PullUp pullup_4 (.out(DLEN[2]));
  PullDown pulldown_2 (.out(DLEN[3]));
  HEF4557B hef4557b_1 (
    .DA(multiplexer_1_out), .DB(d_ff_as_1_q), .A_nB(nOUTPUT_SH), .nCP1(1'b0), .CP0(CLK), .MR(RESET_SH),
    .L32(DLEN[5]), .L16(DLEN[4]), .L8(DLEN[3]), .L4(DLEN[2]), .L2(DLEN[1]), .L1(DLEN[0]), .VCC(1'b1),
    .GND(1'b0), .Q(OUT_SH));  // open: nQ
endmodule

/* Test case:
CLK ~{L}A RESET_SH ~OUTPUT_SH IN_SH       LENIN_SH       LOADLEN_SH OUT_SH    DLEN

loop (rep,32)

# SRA

let A = random(1<<32);
let L = 3;
let R = (A >> (31 - L));

# Load shift length

loop (i,32)
0   1    0         1          0           (L>>i&1)       1          X         X
1   1    0         1          0           (L>>i&1)       1          X         X
end loop

# Latch length
0   1    1         1          0           0              0          X         X
0   1    0         1          0           0              0          X         X

# Load argument
loop (i,32)
0   1    0         1          (A>>i&1)    0              0          X         X
1   1    0         1          (A>>i&1)    0              0          X         X
end loop

# Output result
loop (i,3)
0   1    0         0          0           0              0          (R>>i&1)  X
1   1    0         0          0           0              0          X         X
end loop

loop (i,32-3)
0   1    0         0          0           0              0          (A>>31&1) X
1   1    0         0          0           0              0          X         X
end loop

# SLL

let A = random(1<<32);
let dL = random(32);

let L = 32 + dL;
let R = (A << (L - 31));
loop (i,32)
0   0    0         1          0           (L>>i&1)       1          X         X
1   0    0         1          0           (L>>i&1)       1          X         X
end loop
0   0    1         1          0           0              0          X         X
0   0    0         1          0           0              0          X         X
loop (i,32)
0   0    0         1          (A>>i&1)    0              0          X         X
1   0    0         1          (A>>i&1)    0              0          X         X
end loop
loop (i,32)
0   0    0         0          0           0              0          (R>>i&1)  X
1   0    0         0          0           0              0          X         X
end loop

# SRL

let L = dL;
let R = (A >> (31 - L));

loop (i,32)
0   0    0         1          0           (L>>i&1)       1          X         X
1   0    0         1          0           (L>>i&1)       1          X         X
end loop
0   0    1         1          0           0              0          X         X
0   0    0         1          0           0              0          X         X
loop (i,32)
0   0    0         1          (A>>i&1)    0              0          X         X
1   0    0         1          (A>>i&1)    0              0          X         X
end loop
loop (i,32)
0   0    0         0          0           0              0          (R>>i&1)  X
1   0    0         0          0           0              0          X         X
end loop

end loop
*/
