// Digital circuit CSR-address.dig as structural Verilog
module CSR_address (
  input  CLK,
  input  IN,
  input  LATCH,
  input  nRESET,
  output [11:0] OUT
);

  wire _74595_1_p1;

  // _74595 _74595_1: pin names not known; wires that end beside it: _74595_1_p1, CLK, nRESET, LATCH, 1'b0, 1'b1, 1'b0, OUT[0], OUT[1], OUT[2], OUT[3], OUT[4], OUT[5], OUT[6], OUT[7]
  // _74595 _74595_2: pin names not known; wires that end beside it: IN, CLK, nRESET, LATCH, 1'b0, 1'b1, 1'b0, OUT[8], OUT[9], OUT[10], OUT[11], _74595_1_p1
endmodule
