// Digital circuit Mem-decode.dig as structural Verilog
module Mem_decode (
  input  [31:0] ADDR,
  input  [7:0] IN,
  input  nOE,
  input  nWE,
  input  [7:0] ROM_DATA,
  output [7:0] OUT,
  output [15:0] ROM_ADDR,
  output ROM_SEL
);

  wire demultiplexer_1_out_0, demultiplexer_1_out_2, demultiplexer_1_out_3, or_1_out;

  assign OUT = ~nWE ? IN : 8'bz;  // DriverInvSel driverinvsel_1
  Demultiplexer #(.Selector_Bits(2), .Default(1)) demultiplexer_1 (
    .sel(ADDR[31:30]), .in(1'b0), .out_0(demultiplexer_1_out_0), .out_2(demultiplexer_1_out_2),
    .out_3(demultiplexer_1_out_3));  // open: out_1
  RAMSinglePortSel #(.AddrBits(16), .Bits(8)) RAM (
    .A(ADDR[15:0]), .CS(~demultiplexer_1_out_2), .WE(~nWE), .OE(~nOE), .D(OUT));
  not not_1 (ROM_SEL, demultiplexer_1_out_0);
  or or_1 (or_1_out, demultiplexer_1_out_0, nOE);
  assign OUT = ~or_1_out ? ROM_DATA : 8'bz;  // DriverInvSel driverinvsel_2

  assign ROM_ADDR = ADDR[15:0];
endmodule

/* Test case:
ADDR       ~OE ~WE IN          OUT

0x00000000 1   1   Z           Z
0x00000000 0   1   Z           0x00
0x00000010 0   1   Z           0x10
0x000000AA 0   1   Z           0xAA
0x0000001F 0   1   Z           0x1F

0x80000000 1   0   0xDE        X
0x80000010 1   0   0xAD        X
0x80000000 0   1   Z           0xDE
0x80000010 0   1   Z           0xAD
0x4000001F 0   1   Z           Z
*/
