// Digital circuit Mem.dig as structural Verilog
module Mem (
  input  CLK,
  input  BUS_CLK,
  input  IN,
  input  ADDR_IN,
  input  ADDR_LATCH,
  input  ADDR_CLK,
  input  nOE,
  input  nWE,
  input  nS_EXT,
  input  nRESET,
  input  [7:0] DIn,
  output OUT,
  output [7:0] DATA,
  output [31:0] DATA_ADDR,
  output [31:0] DAddr,
  output [7:0] DVal,
  output nMEM_OE_OUT,
  output nMEM_WE_OUT
);

  wire d_ff_1_nq, d_ff_2_nq, d_ff_3_nq, d_ff_as_1_nq, d_ff_as_1_q, SIGN;

  D_FF_AS d_ff_as_1 (.Set(~nRESET), .D(nWE), .C(CLK), .Clr(~nWE), .Q(d_ff_as_1_q), .nQ(d_ff_as_1_nq));
  D_FF #(.Default(1)) d_ff_1 (.D(ADDR_LATCH), .C(CLK), .nQ(d_ff_1_nq));  // open: Q
  // _74595 _74595_1: pin names not known; wires that end beside it: IN, BUS_CLK, nRESET, d_ff_as_1_nq, d_ff_as_1_q, DIn[0], DIn[1], DIn[2], DIn[3], DIn[4], DIn[5], DIn[6], DIn[7]
  Mem_addr mem_addr_1 (
    .CLK(BUS_CLK), .IN(ADDR_IN), .LATCH(ADDR_LATCH), .ADDR_CLK(ADDR_CLK), .nPE(d_ff_1_nq), .nRESET(nRESET),
    .ADDR(DAddr));
  PullDown #(.Bits(8)) pulldown_1 (.out(DIn));
  D_FF #(.Default(1)) d_ff_2 (.D(nOE), .C(CLK), .nQ(d_ff_2_nq));  // open: Q
  D_FF #(.Default(1)) d_ff_3 (.D(DIn[7]), .C(d_ff_2_nq), .nQ(d_ff_3_nq));  // open: Q
  nor nor_1 (SIGN, nS_EXT, d_ff_3_nq);
  // _74597 _74597_1: pin names not known; wires that end beside it: nRESET, BUS_CLK, SIGN, d_ff_2_nq, nOE, DIn[0], DIn[1], DIn[2], DIn[3], DIn[4], DIn[5], DIn[6], DIn[7], OUT, DVal

  assign DATA = DIn;
  assign DATA_ADDR = DAddr;
  assign nMEM_OE_OUT = nOE;
  assign nMEM_WE_OUT = nWE;

  // Notes on the sheet:
  //   nOE: default 1
  //   nWE: default 1
  //   Can also set RCLK to 
  //   ~{WE} through an inverter
  //   if FF has no ~{Q} output
endmodule

/* Test case Address:
CLK  BUS-CLK ADDR-IN      ADDR-LATCH ADDR-CLK IN       ~OE ~WE ~{S-EXT} ~RESET DIn      DATA-ADDR    

0    0       0            0          0        0        1   1   1        0      Z        X    
0    0       0            0          0        0        1   1   1        0      Z        X    

loop (rep,32)

let addr = random(1<<32);

# Output address
loop (i,32)
0    0       (addr>>i&1)  0          0        0         1  1   1        1      Z        X    
1    1       (addr>>i&1)  0          0        0         1  1   1        1      Z        X    
end loop

# Latch address
0    0       0            1          0        0         1  1   1        1      Z        X    
1    0       0            1          0        0         1  1   1        1      Z        X    

# Output address
0    0       0            0          1        0         1  1   1        1      Z        X    
1    0       0            0          1        0         1  1   1        1      Z        X    

# Check address
0    0       0            0          0        0         1  1   1        1      Z        (addr)  
1    0       0            0          0        0         1  1   1        1      Z        (addr)  

# Increment address
0    0       0            0          1        0         1  1   1        1      Z        X    
1    0       0            0          1        0         1  1   1        1      Z        X    

# Check address
0    0       0            0          0        0         1  1   1        1      Z        (addr+1)
1    0       0            0          0        0         1  1   1        1      Z        (addr+1)

# Increment address
0    0       0            0          1        0         1  1   1        1      Z        X    
1    0       0            0          1        0         1  1   1        1      Z        X    

# Check address
0    0       0            0          0        0         1  1   1        1      Z        (addr+2)
1    0       0            0          0        0         1  1   1        1      Z        (addr+2)

end loop
*/

/* Test case Data Out:
CLK  BUS-CLK ADDR-IN      ADDR-LATCH ADDR-CLK IN       ~OE ~WE ~{S-EXT} ~RESET DIn      OUT        DVal

0    0       0            0          0        0        1   1   1        0      Z        X          X

loop (rep,32)

# Not sign extended

let d = random(1<<8);

# Output address
0    0       0            0          0        0         1  1   1        1      Z        X          X
1    1       0            0          0        0         1  1   1        1      Z        X          X

# Latch address
0    0       0            1          0        0         1  1   1        1      Z        X          X
1    0       0            1          0        0         1  1   1        1      Z        X          X

# Output address
0    0       0            0          1        0         1  1   1        1      Z        X          X
1    0       0            0          1        0         1  1   1        1      Z        X          X

# Output data
0    0       0            0          1        0         0  1   1        1      (d)      X          X
1    0       0            0          1        0         0  1   1        1      (d)      X          X

# Shift out data
loop (i,8)
0    0       0            0          1        0         1  1   1        1      Z        ((d>>i)&1) X
1    1       0            0          1        0         1  1   1        1      Z        X          X
end loop

# Check sign bit

0    0       0            0          1        0         1  1   1        1      Z        0          X
1    0       0            0          1        0         1  1   1        1      Z        X          X

# Sign extended positive

let s = 0;
let d = (s << 7) | random(1<<7);

# Output address
0    0       0            0          0        0         1  1   0        1      Z        X          X
1    1       0            0          0        0         1  1   0        1      Z        X          X

# Latch address
0    0       0            1          0        0         1  1   0        1      Z        X          X
1    0       0            1          0        0         1  1   0        1      Z        X          X

# Output address
0    0       0            0          1        0         1  1   0        1      Z        X          X
1    0       0            0          1        0         1  1   0        1      Z        X          X

# Output data
0    0       0            0          1        0         0  1   0        1      (d)      X          X
1    0       0            0          1        0         0  1   0        1      (d)      X          X

# Shift out data
loop (i,8)
0    0       0            0          1        0         1  1   0        1      Z        ((d>>i)&1) X
1    1       0            0          1        0         1  1   0        1      Z        X          X
end loop

# Check sign bit

0    0       0            0          1        0         1  1   0        1      Z        (s)        X
1    0       0            0          1        0         1  1   0        1      Z        X          X


# Sign extended negative

let s = 1;
let d = (s << 7) | random(1<<7);

# Output address
0    0       0            0          0        0         1  1   0        1      Z        X          X
1    1       0            0          0        0         1  1   0        1      Z        X          X

# Latch address
0    0       0            1          0        0         1  1   0        1      Z        X          X
1    0       0            1          0        0         1  1   0        1      Z        X          X

# Output address
0    0       0            0          1        0         1  1   0        1      Z        X          X
1    0       0            0          1        0         1  1   0        1      Z        X          X

# Output data
0    0       0            0          1        0         0  1   0        1      (d)      X          X
1    0       0            0          1        0         0  1   0        1      (d)      X          X

# Shift out data
loop (i,8)
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*/

/* Test case Data In:
CLK  BUS-CLK ADDR-IN      ADDR-LATCH ADDR-CLK IN         ~OE ~WE ~{S-EXT} ~RESET DIn      DATA

0    0       0            0          0        0          1   1   1        0      Z        X

loop (rep,32)

let d = random(1<<8);

# Clock in data

loop (i,8)
0    0       0            0          0        ((d>>i)&1) 1   1   1        1      Z        X
1    1       0            0          0        ((d>>i)&1) 1   1   1        1      Z        X
end loop

# Output data
0    0       0            0          0        0          1   0   1        1      Z        X
1    0       0            0          0        0          1   0   1        1      Z        (d)

# Check data

0    0       0            0          0        0          1   1   1        1      Z        (d)
1    0       0            0          0        0          1   1   1        1      Z        X

end loop
*/
