// Digital circuit OpCode.dig as structural Verilog
module OpCode (
  input  CLK,
  input  IN,
  input  LATCH_OP,
  input  nRESET,
  input  LATCH_IMM,
  input  SnP_IMM,
  output ImmI,
  output ImmS,
  output ImmB,
  output ImmU,
  output ImmJ,
  output Const31,
  output ImmCSR,
  output [3:0] RSA,
  output [3:0] RSB,
  output [3:0] RSD,
  output [2:0] FUNC3,
  output [4:0] OPCODE,
  output SA_ALU
);

  wire _74hc595_2_qh_2, _74hc595_3_qh_2, _74hc595_4_qh_2, B0, B1, B11, B19, B24, B25, B26, B27, B28, B29, B31;

  _74HC595 _74hc595_1 (
    .SER(_74hc595_2_qh_2), .SRCLK(CLK), .nSRCLR(nRESET), .RCLK(LATCH_OP), .nOE(1'b0), .VCC(1'b1), .GND(1'b0),
    .QH(B0), .QG(B1), .QF(OPCODE[0]), .QE(OPCODE[1]), .QD(OPCODE[2]), .QC(OPCODE[3]), .QB(OPCODE[4]),
    .QA(RSD[0]));  // open: QH_2
  _74HC595 _74hc595_2 (
    .SER(_74hc595_3_qh_2), .SRCLK(CLK), .nSRCLR(nRESET), .RCLK(LATCH_OP), .nOE(1'b0), .VCC(1'b1), .GND(1'b0),
    .QH(RSD[1]), .QG(RSD[2]), .QF(RSD[3]), .QE(B11), .QD(FUNC3[0]), .QC(FUNC3[1]), .QB(FUNC3[2]),
    .QA(RSA[0]), .QH_2(_74hc595_2_qh_2));
  _74HC595 _74hc595_3 (
    .SER(_74hc595_4_qh_2), .SRCLK(CLK), .nSRCLR(nRESET), .RCLK(LATCH_OP), .nOE(1'b0), .VCC(1'b1), .GND(1'b0),
    .QH(RSA[1]), .QG(RSA[2]), .QF(RSA[3]), .QE(B19), .QD(RSB[0]), .QC(RSB[1]), .QB(RSB[2]), .QA(RSB[3]),
    .QH_2(_74hc595_3_qh_2));
  _74HC595 _74hc595_4 (
    .SER(IN), .SRCLK(CLK), .nSRCLR(nRESET), .RCLK(LATCH_OP), .nOE(1'b0), .VCC(1'b1), .GND(1'b0), .QH(B24),
    .QG(B25), .QF(B26), .QE(B27), .QD(B28), .QC(B29), .QB(SA_ALU), .QA(B31), .QH_2(_74hc595_4_qh_2));
  Imm16 u_ImmI (
    .CLK(CLK), .nRESET(nRESET), .LATCH(LATCH_IMM), .SnP(SnP_IMM),
    .Val({{5{B31}}, SA_ALU, B29, B28, B27, B26, B25, B24, RSB}), .OUT(ImmI));
  Imm16 u_ImmS (
    .CLK(CLK), .nRESET(nRESET), .LATCH(LATCH_IMM), .SnP(SnP_IMM),
    .Val({{5{B31}}, SA_ALU, B29, B28, B27, B26, B25, B11, RSD}), .OUT(ImmS));
  Imm16 u_ImmB (
    .CLK(CLK), .nRESET(nRESET), .LATCH(LATCH_IMM), .SnP(SnP_IMM),
    .Val({{4{B31}}, RSD[0], SA_ALU, B29, B28, B27, B26, B25, B11, RSD[3:1], 1'b0}), .OUT(ImmB));
  Imm32 u_ImmU (
    .CLK(CLK), .nRESET(nRESET), .LATCH(LATCH_IMM), .SnP(SnP_IMM),
    .Val({B31, SA_ALU, B29, B28, B27, B26, B25, B24, RSB, B19, RSA, FUNC3, {12{1'b0}}}), .OUT(ImmU));
  Imm24 u_ImmJ (
    .CLK(CLK), .nRESET(nRESET), .LATCH(LATCH_IMM), .SnP(SnP_IMM),
    .Val({{5{B31}}, B19, RSA, FUNC3, SA_ALU, B29, B28, B27, B26, B25, B24, RSB[3:1], 1'b0}), .OUT(ImmJ));
  Imm8 u_Const31 (.CLK(CLK), .nRESET(nRESET), .LATCH(LATCH_IMM), .SnP(SnP_IMM), .Val(8'h1f), .OUT(Const31));
  Imm8 u_ImmCSR (.CLK(CLK), .nRESET(nRESET), .LATCH(LATCH_IMM), .SnP(SnP_IMM), .Val({3'b000, B19, RSA}), .OUT(ImmCSR));

  // Other names for the same wires on the sheet: B2 = OPCODE[0]; B3 = OPCODE[1]; B4 = OPCODE[2]; B5 = OPCODE[3];
  //   B6 = OPCODE[4]; B7 = RSD[0]; B8 = RSD[1]; B9 = RSD[2]; B10 = RSD[3]; B12 = FUNC3[0]; B13 = FUNC3[1];
  //   B14 = FUNC3[2]; B15 = RSA[0]; B16 = RSA[1]; B17 = RSA[2]; B18 = RSA[3]; B20 = RSB[0]; B21 = RSB[1];
  //   B22 = RSB[2]; B23 = RSB[3]; B30 = SA_ALU; LATCH_IM = LATCH_IMM; SP_IMM = SnP_IMM
endmodule

/* Test case ADD/ADDI/BEQ:
CLK IN           ~RESET LATCH_OP LATCH_IMM S~P_IMM     ImmI        ImmB        RSA   RSB   RSD   FUNC3   OPCODE  SA_ALU

loop (rep, 32)

# Bin immediate

let imm = random(1<<12);
let s = (imm >> 11) & 1;
let op = 0b00100;
let func3 = random(8);
let rd = random(16);
let rs1 = random(16);

let instr = ((imm << 20) | (rs1 << 15) | (func3 << 12) | (rd << 7) | (op << 2) | 0b11) & 0xFFFFFFFF;

0   0            0      0        0         1           X           X           X     X     X     X       X       X

loop (i,32)
0   (instr>>i&1) 1      0        0         0           X           X           X     X     X     X       X       X
1   (instr>>i&1) 1      0        0         0           X           X           X     X     X     X       X       X
end loop

0   0            1      1        0         0           X           X           X     X     X     X       X       X
1   0            1      1        0         0           X           X           X     X     X     X       X       X

0   0            1      0        1         0           X           X           X     X     X     X       X       X
1   0            1      0        1         0           X           X           (rs1) X     (rd)  (func3) (op)    X

loop (i,12)
0   0            1      0        0         1           (imm>>i&1)  X           X     X     X     X       X       X
1   0            1      0        0         1           X           X           X     X     X     X       X       X
end loop

loop (i,20)
0   0            1      0        0         1           (s)         X           X     X     X     X       X       X
1   0            1      0        0         1           X           X           X     X     X     X       X       X
end loop


# SUB

let s = (imm >> 11) & 1;
let op = 0b01100;
let func3 = 000;
let rd = random(16);
let rs1 = random(16);
let rs2 = random(16);

let instr = ((0b0100000 << 25) | (rs2 << 20) | (rs1 << 15) | (func3 << 12) | (rd << 7) | (op << 2) | 0b11) & 0xFFFFFFFF;

0   0            0      0        0         1           X           X           X     X     X     X       X       X

loop (i,32)
0   (instr>>i&1) 1      0        0         0           X           X           X     X     X     X       X       X
1   (instr>>i&1) 1      0        0         0           X           X           X     X     X     X       X       X
end loop

0   0            1      1        0         0           X           X           X     X     X     X       X       X
1   0            1      1        0         0           X           X           X     X     X     X       X       X

0   0            1      0        1         0           X           X           X     X     X     X       X       X
1   0            1      0        1         0           X           X           (rs1) (rs2) (rd)  (func3) (op)    1

# BEQ

let imm12 = random(1<<1);
let imm10to5 = random(1<<6);
let imm4to1 = random(1<<4);
let imm11 = random(1<<1);
let rs1 = random(1<<4);
let rs2 = random(1<<4);
let funct3 = 0;
let op = 0b11000;

let imm = (imm12 << 12) | (imm11 << 11) | (imm10to5 << 5) | (imm4to1 << 1);
let s = (imm >> 12) & 1;

let instr = (imm12 << 31) | (imm10to5 << 25) | (rs2 << 20) | (rs1 << 15) | (funct3 << 12) | (imm4to1 << 8) | (imm11 << 7) | (op << 2) | (0b11);

0   0            0      0        0         1           X           X           X     X     X     X       X       X

loop (i,32)
0   (instr>>i&1) 1      0        0         0           X           X           X     X     X     X       X       X
1   (instr>>i&1) 1      0        0         0           X           X           X     X     X     X       X       X
end loop

0   0            1      1        0         0           X           X           X     X     X     X       X       X
1   0            1      1        0         0           X           X           X     X     X     X       X       X

0   0            1      0        1         0           X           X           X     X     X     X       X       X
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*/
