// Digital circuit PC.dig as structural Verilog
module PC (
  input  CLK,
  input  BUS_CLK,
  input  IN,
  input  IN_LATCH,
  input  OUT_LATCH,
  input  OUT_SnP,
  input  CNT_EN,
  input  nRESET,
  output OUT,
  output [31:0] PC
);

  wire _74hc595_1_qa, _74hc595_1_qb, _74hc595_1_qc, _74hc595_1_qd, _74hc595_1_qe, _74hc595_1_qf,
       _74hc595_1_qg, _74hc595_2_qa, _74hc595_2_qb, _74hc595_2_qc, _74hc595_2_qd, _74hc595_2_qe,
       _74hc595_2_qf, _74hc595_2_qg, _74hc595_2_qh, _74hc595_2_qh_2, _74hc595_3_qa, _74hc595_3_qb,
       _74hc595_3_qc, _74hc595_3_qd, _74hc595_3_qe, _74hc595_3_qf, _74hc595_3_qg, _74hc595_3_qh,
       _74hc595_3_qh_2, _74hc595_4_qa, _74hc595_4_qb, _74hc595_4_qc, _74hc595_4_qd, _74hc595_4_qe,
       _74hc595_4_qf, _74hc595_4_qg, _74hc595_4_qh, _74hc595_4_qh_2, _74hc597_2_q7, _74hc597_3_q7,
       _74hc597_4_q7, _74161_1_p12, _74161_2_p12, _74161_3_p12, _74161_4_p12, _74161_5_p12, _74161_6_p12,
       _74161_7_p12, not_1_out, or_1_out;

  not not_1 (not_1_out, IN_LATCH);
  _74HC595 _74hc595_1 (
    .SER(_74hc595_2_qh_2), .SRCLK(BUS_CLK), .nSRCLR(nRESET), .RCLK(IN_LATCH), .nOE(1'b0), .VCC(1'b1),
    .GND(1'b0), .QG(_74hc595_1_qg), .QF(_74hc595_1_qf), .QE(_74hc595_1_qe), .QD(_74hc595_1_qd),
    .QC(_74hc595_1_qc), .QB(_74hc595_1_qb), .QA(_74hc595_1_qa));  // open: QH, QH_2
  _74HC595 _74hc595_2 (
    .SER(_74hc595_3_qh_2), .SRCLK(BUS_CLK), .nSRCLR(nRESET), .RCLK(IN_LATCH), .nOE(1'b0), .VCC(1'b1),
    .GND(1'b0), .QH(_74hc595_2_qh), .QG(_74hc595_2_qg), .QF(_74hc595_2_qf), .QE(_74hc595_2_qe),
    .QD(_74hc595_2_qd), .QC(_74hc595_2_qc), .QB(_74hc595_2_qb), .QA(_74hc595_2_qa), .QH_2(_74hc595_2_qh_2));
  _74HC595 _74hc595_3 (
    .SER(_74hc595_4_qh_2), .SRCLK(BUS_CLK), .nSRCLR(nRESET), .RCLK(IN_LATCH), .nOE(1'b0), .VCC(1'b1),
    .GND(1'b0), .QH(_74hc595_3_qh), .QG(_74hc595_3_qg), .QF(_74hc595_3_qf), .QE(_74hc595_3_qe),
    .QD(_74hc595_3_qd), .QC(_74hc595_3_qc), .QB(_74hc595_3_qb), .QA(_74hc595_3_qa), .QH_2(_74hc595_3_qh_2));
  _74HC595 _74hc595_4 (
    .SER(IN), .SRCLK(BUS_CLK), .nSRCLR(nRESET), .RCLK(IN_LATCH), .nOE(1'b0), .VCC(1'b1), .GND(1'b0),
    .QH(_74hc595_4_qh), .QG(_74hc595_4_qg), .QF(_74hc595_4_qf), .QE(_74hc595_4_qe), .QD(_74hc595_4_qd),
    .QC(_74hc595_4_qc), .QB(_74hc595_4_qb), .QA(_74hc595_4_qa), .QH_2(_74hc595_4_qh_2));
  or or_1 (or_1_out, CLK, not_1_out);
  D_FF_AS d_ff_as_1 (.Set(1'b0), .D(_74hc595_1_qg), .C(or_1_out), .Clr(~nRESET), .Q(PC[1]));  // open: nQ
  // _74161 _74161_1: pin names not known; wires that end beside it: not_1_out, nRESET, CLK, 1'b1, CNT_EN, _74hc595_1_qf, _74hc595_1_qe, _74hc595_1_qd, _74hc595_1_qc, 1'b1, 1'b0, _74161_1_p12, PC[2], PC[3], PC[4], PC[5]
  // _74161 _74161_2: pin names not known; wires that end beside it: not_1_out, nRESET, CLK, _74161_1_p12, CNT_EN, _74hc595_1_qb, _74hc595_1_qa, _74hc595_2_qh, _74hc595_2_qg, 1'b1, 1'b0, _74161_2_p12, PC[6], PC[7], PC[8], PC[9]
  // _74161 _74161_3: pin names not known; wires that end beside it: not_1_out, nRESET, CLK, _74161_2_p12, CNT_EN, _74hc595_2_qf, _74hc595_2_qe, _74hc595_2_qd, _74hc595_2_qc, 1'b1, 1'b0, _74161_3_p12, PC[10], PC[11], PC[12], PC[13]
  // _74161 _74161_4: pin names not known; wires that end beside it: not_1_out, nRESET, CLK, _74161_3_p12, CNT_EN, _74hc595_2_qb, _74hc595_2_qa, _74hc595_3_qh, _74hc595_3_qg, 1'b1, 1'b0, _74161_4_p12, PC[14], PC[15], PC[16], PC[17]
  // _74161 _74161_5: pin names not known; wires that end beside it: not_1_out, nRESET, CLK, _74161_4_p12, CNT_EN, _74hc595_3_qf, _74hc595_3_qe, _74hc595_3_qd, _74hc595_3_qc, 1'b1, 1'b0, _74161_5_p12, PC[18], PC[19], PC[20], PC[21]
  // _74161 _74161_6: pin names not known; wires that end beside it: not_1_out, nRESET, CLK, _74161_5_p12, CNT_EN, _74hc595_3_qb, _74hc595_3_qa, _74hc595_4_qh, _74hc595_4_qg, 1'b1, 1'b0, _74161_6_p12, PC[22], PC[23], PC[24], PC[25]
  // _74161 _74161_7: pin names not known; wires that end beside it: not_1_out, nRESET, CLK, _74161_6_p12, CNT_EN, _74hc595_4_qf, _74hc595_4_qe, _74hc595_4_qd, _74hc595_4_qc, 1'b1, 1'b0, _74161_7_p12, PC[26], PC[27], PC[28], PC[29]
  // _74161 _74161_8: pin names not known; wires that end beside it: not_1_out, nRESET, CLK, _74161_7_p12, CNT_EN, _74hc595_4_qb, _74hc595_4_qa, 1'b0, 1'b0, 1'b1, 1'b0, PC[30], PC[31]
  _74HC597 _74hc597_1 (
    .nMR(nRESET), .SHCP(BUS_CLK), .DS(_74hc597_2_q7), .STCP(OUT_LATCH), .nPL(OUT_SnP), .D7(1'b0), .D6(PC[1]),
    .D5(PC[2]), .D4(PC[3]), .D3(PC[4]), .D2(PC[5]), .D1(PC[6]), .D0(PC[7]), .Q7(OUT));  // open: Val
  _74HC597 _74hc597_2 (
    .nMR(nRESET), .SHCP(BUS_CLK), .DS(_74hc597_3_q7), .STCP(OUT_LATCH), .nPL(OUT_SnP), .D7(PC[8]),
    .D6(PC[9]), .D5(PC[10]), .D4(PC[11]), .D3(PC[12]), .D2(PC[13]), .D1(PC[14]), .D0(PC[15]),
    .Q7(_74hc597_2_q7));  // open: Val
  _74HC597 _74hc597_3 (
    .nMR(nRESET), .SHCP(BUS_CLK), .DS(_74hc597_4_q7), .STCP(OUT_LATCH), .nPL(OUT_SnP), .D7(PC[16]),
    .D6(PC[17]), .D5(PC[18]), .D4(PC[19]), .D3(PC[20]), .D2(PC[21]), .D1(PC[22]), .D0(PC[23]),
    .Q7(_74hc597_3_q7));  // open: Val
  _74HC597 _74hc597_4 (
    .nMR(nRESET), .SHCP(BUS_CLK), .DS(1'b0), .STCP(OUT_LATCH), .nPL(OUT_SnP), .D7(PC[24]), .D6(PC[25]),
    .D5(PC[26]), .D4(PC[27]), .D3(PC[28]), .D2(PC[29]), .D1(PC[30]), .D0(PC[31]), .Q7(_74hc597_4_q7));  // open: Val

  assign PC[0] = 1'b0;
endmodule

/* Test case:
CLK BUS-CLK IN         IN-LATCH OUT-LATCH OUT-S~P CNT-EN ~{CNT-PE} ~RESET   OUT

loop (rep, 32)

let PC = random(1<<31) << 1;

0   0       0          0        0         0       0      1         0       X

# Input PC

loop (i,32)
0   0       (PC>>i&1)  0        0         0       0      1         1       X
1   1       (PC>>i&1)  0        0         0       0      1         1       X
end loop

# Latch in

0   0       0          1        0         0       1      0         1       X
1   0       0          1        0         0       1      0         1       X

# Latch out and load

0   0       0          0        1         0       0      1         1       X
1   0       0          0        1         0       0      1         1       X

# Output PC

loop (i,32)
0   0       0          0        0         1       0      1         1       (PC>>i&1)
1   1       0          0        0         1       0      1         1       X
end loop

# Increase PC

0   0       0          0        0         0       1      1         1       X
1   0       0          0        0         0       1      1         1       X

# Output old PC

loop (i,32)
0   0       0          0        0         1       0      1         1       (PC>>i&1)
1   1       0          0        0         1       0      1         1       X
end loop

# Latch out and load new PC

0   0       0          0        1         0       0      1         1       X
1   0       0          0        1         0       0      1         1       X

# Output PC

loop (i,32)
0   0       0          0        0         1       0      1         1       ((PC+4)>>i&1)
1   1       0          0        0         1       0      1         1       X
end loop

end loop
*/
