// Digital circuit Register-bank.dig as structural Verilog
module Register_bank (
  input  BUS_CLK,
  input  IN,
  input  nIN_EN,
  input  [3:0] SA,
  input  [3:0] SB,
  input  [3:0] SD,
  input  RESET,
  output A,
  output B
);

  wire demultiplexer_1_out_0, demultiplexer_1_out_1, not_1_out, not_2_out;

  Demultiplexer #(.Default(1)) demultiplexer_1 (
    .sel(SD[3]), .in(nIN_EN), .out_0(demultiplexer_1_out_0), .out_1(demultiplexer_1_out_1));
  not not_1 (not_1_out, SA[3]);
  Register_bank_0 register_bank_0_1 (
    .BUS_CLK(BUS_CLK), .IN(IN), .SA(SA[2:0]), .SB(SB[2:0]), .SD(SD[2:0]), .nIN_EN(demultiplexer_1_out_0),
    .nA_EN(SA[3]), .nB_EN(SB[3]), .RESET(RESET), .A(A), .B(B));
  Register_bank_8 register_bank_8_1 (
    .BUS_CLK(BUS_CLK), .IN(IN), .SA(SA[2:0]), .SB(SB[2:0]), .SD(SD[2:0]), .nIN_EN(demultiplexer_1_out_1),
    .nA_EN(not_1_out), .nB_EN(not_2_out), .RESET(RESET), .A(A), .B(B));
  not not_2 (not_2_out, SB[3]);

  // Other names for the same wires on the sheet: SA012[2:0] = SA[2:0]; SB012[2:0] = SB[2:0]; SD012[2:0] = SD[2:0]
endmodule

/* Test case:
BUS-CLK IN        ~{IN-EN} RESET SA   SB   SD     A        B

loop (rep,32)

let R1 = 1 + random(14);
let R2 = R1 + 1 + random(15 - R1);

let A = random(1<<32);
let B = random(1<<32);


0   0         1        1     0    0    0      0        0

loop (i,32)
0   (A>>i&1)  0        0     0    0    (R1)   0        0
1   (A>>i&1)  0        0     0    0    (R1)   X        X
end loop

loop (i,32)
0   (B>>i&1)  0        0     (R1) 0    (R2)   (A>>i&1) 0
1   (B>>i&1)  0        0     (R1) 0    (R2)   X        X
end loop

loop (i,32)
0   0         1        0     (R1) (R2) 0      (A>>i&1) (B>>i&1)
1   0         1        0     (R1) (R2) 0      X        X
end loop

end loop
*/
